// Logisim project arch-circuits.circ as structural Verilog: 7 circuits, main circuit full-adder explanation
module full_adder_explanation (
  input  A_i__x___bit_of_value_1,
  input  B_i__y___bit_of_value_2,
  input  C_i__z___carry,
  input  A_i__x___bit_of_value_1_2,
  input  B_i__y___bit_of_value_2_2,
  input  C_i__z___carry_2,
  input  A_i__x___bit_of_value_1_3,
  input  B_i__y___bit_of_value_2_3,
  input  C_i__z___carry_3,
  input  A_i__x___bit_of_value_1_4,
  input  A_i__x___bit_of_value_1_5,
  input  B_i__y___bit_of_value_2_4,
  input  B_i__y___bit_of_value_2_5,
  input  C_i__z___carry_4,
  input  C_i__z___carry_5,
  input  A_i__x___bit_of_value_1_6,
  input  B_i__y___bit_of_value_2_6,
  input  C_i__z___carry_6
);

  wire and_z_2_out, and_z_3_out, and_z_out, or_1_out, or_2_out, or_3_out, or_4_out, x_and_y_2_out,
       x_and_y_3_out, x_and_y_4_out, x_and_y_out, x_and_z_out, x_xor_y_2_out, x_xor_y_3_out, x_xor_y_4_out,
       x_xor_y_5_out, x_xor_y_out, xor_z_2_out, xor_z_3_out, xor_z_out, y_and_z_out;

  and x_and_z (x_and_z_out, A_i__x___bit_of_value_1_2, C_i__z___carry_2);
  and x_and_y (x_and_y_out, A_i__x___bit_of_value_1_2, B_i__y___bit_of_value_2_2);
  and y_and_z (y_and_z_out, B_i__y___bit_of_value_2_2, C_i__z___carry_2);
  xor x_xor_y (x_xor_y_out, A_i__x___bit_of_value_1_3, B_i__y___bit_of_value_2_3);
  xor x_xor_y_2 (x_xor_y_2_out, A_i__x___bit_of_value_1_4, B_i__y___bit_of_value_2_4);
  xor x_xor_y_3 (x_xor_y_3_out, A_i__x___bit_of_value_1, B_i__y___bit_of_value_2);
  and and_z (and_z_out, x_xor_y_out, C_i__z___carry_3);
  and x_and_y_2 (x_and_y_2_out, A_i__x___bit_of_value_1_3, B_i__y___bit_of_value_2_3);
  LED S__result_bit (.in(xor_z_out));
  xor xor_z (xor_z_out, x_xor_y_2_out, C_i__z___carry_4);
  LED S__result_bit_2 (.in(xor_z_2_out));
  xor xor_z_2 (xor_z_2_out, x_xor_y_3_out, C_i__z___carry);
  or or_1 (or_1_out, x_and_z_out, x_and_y_out, y_and_z_out);
  LED C__carry (.in(or_1_out));
  or or_2 (or_2_out, and_z_out, x_and_y_2_out);
  LED C__carry_2 (.in(or_2_out));
  xor x_xor_y_4 (x_xor_y_4_out, A_i__x___bit_of_value_1_6, B_i__y___bit_of_value_2_6);
  and x_and_y_3 (x_and_y_3_out, A_i__x___bit_of_value_1_6, B_i__y___bit_of_value_2_6);
  and and_z_2 (and_z_2_out, x_xor_y_4_out, C_i__z___carry_6);
  xor xor_z_3 (xor_z_3_out, x_xor_y_4_out, C_i__z___carry_6);
  or or_3 (or_3_out, x_and_y_3_out, and_z_2_out);
  LED S__result_bit_3 (.in(xor_z_3_out));
  LED C__carry_3 (.in(or_3_out));
  xor x_xor_y_5 (x_xor_y_5_out, A_i__x___bit_of_value_1_5, B_i__y___bit_of_value_2_5);
  and and_z_3 (and_z_3_out, x_xor_y_5_out, C_i__z___carry_5);
  and x_and_y_4 (x_and_y_4_out, A_i__x___bit_of_value_1_5, B_i__y___bit_of_value_2_5);
  or or_4 (or_4_out, and_z_3_out, x_and_y_4_out);
  LED C__carry_4 (.in(or_4_out));

  // Notes on the sheet:
  //   Getting summation result bit value (S)
  //   S = x (+) y (+) z
  //   Calculating the next carry (C)
  //   C = xz + xy + yz
  //   Carry can also be calculated with:
  //   C = (x (+) y)z + xy
  //   S
  //   (This is more efficient, since both S and C need "x xor y")
  //   Putting them together:
  //   +
  //   Full adder:
  //   x y z | S C
  //   0 0 0 | 0 0
  //   0 0 1 | 1 0
  //   0 1 0 | 1 0
  //   0 1 1 | 0 1
  //   1 0 0 | 1 0
  //   1 0 1 | 0 1
  //   1 1 0 | 0 1
  //   1 1 1 | 1 1
  //   C
  //   FULL ADDER
  //   x y z | S C
  //   0 0 0 | 0 0
  //   0 0 1 | 1 0
  //   0 1 0 | 1 0
  //   0 1 1 | 0 1
  //   1 0 0 | 1 0
  //   1 0 1 | 0 1
  //   1 1 0 | 0 1
  //   1 1 1 | 1 1
endmodule

module full_adder (
  input  A,
  input  B,
  input  C,
  output S,
  output C_2
);

  wire and_z_out, x_and_y_out, x_xor_y_out;

  xor x_xor_y (x_xor_y_out, A, B);
  and x_and_y (x_and_y_out, A, B);
  xor xor_z (S, x_xor_y_out, C);
  and and_z (and_z_out, x_xor_y_out, C);
  or or_1 (C_2, x_and_y_out, and_z_out);
endmodule

module SR_Latch_explanation (
  input  Reset,
  input  Set,
  input  Set_2,
  input  Reset_2,
  output Q,
  output Q_prime,
  output Q_2,
  output Q_prime_2
);

  wire not_1_out, not_2_out;

  not not_1 (not_1_out, Set_2);
  not not_2 (not_2_out, Reset_2);
  nor _1 (Q, Reset, Q_prime);
  nor _2 (Q_prime, Q, Set);
  nand nand_1 (Q_2, not_1_out, Q_prime_2);
  nand nand_2 (Q_prime_2, Q_2, not_2_out);

  // Notes on the sheet:
  //   The logic still appears to work with NAND gates, as long as you negate each input (and flip set and reset)
  //   changes to that bit - it retains its state)
  //   As soon as an output (Q or Q') is triggered and its output is 1, 
  //   that feeds into the alternate NOR gate, meaning it will turn OFF
  //   ex: Assuming Q is 0 and Q' is 1, if we trigger the set bit,
  //   remembering that a NOR gate turns OFF if any one of the inputs is 1
  //   (regardless of what the other input bit is, meaning it disregards 
  //   NOR gate 2 deactivates, meaning NOR gate 1 has only inputs of 0,
  //   so it now outputs a 1 to Q, which also goes to NOR gate 2 as input.
  //   The output of NOR 2 will now always be 1, regardless of what the set bit is
  //   SR-LATCH
endmodule

module SR_Latch (
  input  Reset,
  input  Set,
  output Q,
  output Q_prime
);

  nor _1 (Q, Reset, Q_prime);
  nor _2 (Q_prime, Q, Set);
endmodule

module D_Latch_explanation (
  input  Data,
  input  Enable,
  output Q,
  output Q_prime
);

  wire _3_out, _4_out, not_1_out, not_2_out;

  not not_1 (not_1_out, Enable);
  not not_2 (not_2_out, Data);
  nor _3 (_3_out, Data, not_1_out);
  nor _4 (_4_out, not_1_out, not_2_out);
  nor _1 (Q, _3_out, Q_prime);
  nor _2 (Q_prime, Q, _4_out);

  // Notes on the sheet:
  //   Again remembering that a NOR gate turns OFF if any one of the inputs is 1
  //   When the enable bit is off, 3 and 4 will ALWAYS output 0, regardless of what the data bit is.
  //   (Thus, the inputs to the SR-latch are always 0, so the Data bit can't affect Q and Q')
  //   D-latch solves the problem of accidentally applying a 1 to both set and reset bits of an SR-Latch
  //   (This is bad because it makes the circuit mathematically incorrect, since both Q and Q' would be 0)
  //   D-Latch is also really cool because it can completely shut off the SR-Latch from input data!
  //   D-LATCH
endmodule

module D_Latch (
  input  Data,
  input  Enable,
  output Q,
  output Q_prime
);

  wire _3_out, _4_out, not_1_out, not_2_out;

  not not_1 (not_1_out, Enable);
  not not_2 (not_2_out, Data);
  nor _3 (_3_out, Data, not_1_out);
  nor _4 (_4_out, not_1_out, not_2_out);
  nor _1 (Q, _3_out, Q_prime);
  nor _2 (Q_prime, Q, _4_out);
endmodule

module D_Flip_Flop_explanation (
  input  Data,
  output Q
);

  wire Clock_out, D_Master_q, not_1_out;

  Clock Clock (.out(Clock_out));
  D_Latch D_Master (.Data(Data), .Enable(Clock_out), .Q(D_Master_q));  // open: Q_prime
  not not_1 (not_1_out, Clock_out);
  D_Latch D_Slave (.Data(D_Master_q), .Enable(not_1_out), .Q(Q));  // open: Q_prime

  // Notes on the sheet:
  //   and no further changes to Data will affect Q
  //   Y
  //   When clock is 0, Data isn't affecting Y, since the enable to D-Master is off
  //   because the enable to D-Slave is now off) Once the clock flips back to 0
  //   (Ctrl-T advances the clock by one tick. Ctrl-K turns on the clock [oscillates once per second by default])
  //   (see Simulate menu for options)
  //   When clock is 1, whatever Data is propagates to Y, (but Q is not yet affected,
  //   (negative edge trigger), Y propagates to Q, since D-Slave is now enabled,
  //   D Flip-Flop
  //   While expensive to make, (8 NOR gates for 1 bit of memory) it is fast and reliable
  //   Referred to as SRAM (Static Random Access Memory) used for CPU cache
endmodule
