// Logisim project cpu.circ as structural Verilog: 3 circuits, main circuit main
module main (
  input  in_1,
  input  in_2,
  input  in_3,
  input  in_4,
  input  in_5,
  input  in_6,
  input  in_7,
  input  in_8,
  input  in_9,
  input  in_10
);

  wire [7:0] register_1_q;

  Register register_1 (
    .D({in_8, in_7, in_6, in_5, in_4, in_3, in_2, in_1}), .en(in_9), .Q(register_1_q), .clk(in_10));  // open: clr
endmodule

module _32_bit_register (
  input  in_1,
  input  in_2,
  input  in_3,
  input  in_4,
  input  in_5,
  input  in_6,
  input  in_7,
  input  in_8,
  input  in_9,
  input  in_10,
  input  in_11,
  input  in_12,
  input  in_13,
  input  in_14,
  input  in_15,
  input  in_16,
  input  in_17,
  input  in_18,
  input  in_19,
  input  in_20,
  input  in_21,
  input  in_22,
  input  in_23,
  input  in_24,
  input  in_25,
  input  in_26,
  input  in_27,
  input  in_28,
  input  in_29,
  input  in_30,
  input  in_31,
  input  in_32,
  input  Clock
);

  D_Flip_Flop d_ff_1 (.clk(Clock), .D(in_1));  // open: Q, Qn, preset, en, reset
  D_Flip_Flop d_ff_2 (.clk(Clock), .D(in_2));  // open: Q, Qn, preset, en, reset
  D_Flip_Flop d_ff_3 (.clk(Clock), .D(in_3));  // open: Q, Qn, preset, en, reset
  D_Flip_Flop d_ff_4 (.clk(Clock));  // open: D, Q, Qn, preset, en, reset
  D_Flip_Flop d_ff_5 (.clk(Clock));  // open: D, Q, Qn, preset, en, reset
  D_Flip_Flop d_ff_6 (.clk(Clock));  // open: D, Q, Qn, preset, en, reset
  D_Flip_Flop d_ff_7 (.clk(Clock));  // open: D, Q, Qn, preset, en, reset
  D_Flip_Flop d_ff_8 (.clk(Clock));  // open: D, Q, Qn, preset, en, reset
  D_Flip_Flop d_ff_9 (.clk(Clock));  // open: D, Q, Qn, preset, en, reset
  D_Flip_Flop d_ff_10 (.clk(Clock));  // open: D, Q, Qn, preset, en, reset
  D_Flip_Flop d_ff_11 (.clk(Clock));  // open: D, Q, Qn, preset, en, reset
  D_Flip_Flop d_ff_12 (.clk(Clock));  // open: D, Q, Qn, preset, en, reset
  D_Flip_Flop d_ff_13 (.clk(Clock));  // open: D, Q, Qn, preset, en, reset
  D_Flip_Flop d_ff_14 (.clk(Clock));  // open: D, Q, Qn, preset, en, reset
  D_Flip_Flop d_ff_15 (.clk(Clock));  // open: D, Q, Qn, preset, en, reset
  D_Flip_Flop d_ff_16 (.clk(Clock));  // open: D, Q, Qn, preset, en, reset
  D_Flip_Flop d_ff_17 (.clk(Clock));  // open: D, Q, Qn, preset, en, reset
  D_Flip_Flop d_ff_18 (.clk(Clock));  // open: D, Q, Qn, preset, en, reset
  D_Flip_Flop d_ff_19 (.clk(Clock));  // open: D, Q, Qn, preset, en, reset
  D_Flip_Flop d_ff_20 (.clk(Clock));  // open: D, Q, Qn, preset, en, reset
  D_Flip_Flop d_ff_21 (.clk(Clock));  // open: D, Q, Qn, preset, en, reset
  D_Flip_Flop d_ff_22 (.clk(Clock));  // open: D, Q, Qn, preset, en, reset
  D_Flip_Flop d_ff_23 (.clk(Clock));  // open: D, Q, Qn, preset, en, reset
  D_Flip_Flop d_ff_24 (.clk(Clock));  // open: D, Q, Qn, preset, en, reset
  D_Flip_Flop d_ff_25 (.clk(Clock));  // open: D, Q, Qn, preset, en, reset
  D_Flip_Flop d_ff_26 (.clk(Clock));  // open: D, Q, Qn, preset, en, reset
  D_Flip_Flop d_ff_27 (.clk(Clock));  // open: D, Q, Qn, preset, en, reset
  D_Flip_Flop d_ff_28 (.clk(Clock));  // open: D, Q, Qn, preset, en, reset
  D_Flip_Flop d_ff_29 (.clk(Clock));  // open: D, Q, Qn, preset, en, reset
  D_Flip_Flop d_ff_30 (.clk(Clock));  // open: D, Q, Qn, preset, en, reset
  D_Flip_Flop d_ff_31 (.clk(Clock));  // open: D, Q, Qn, preset, en, reset
  D_Flip_Flop d_ff_32 (.clk(Clock));  // open: D, Q, Qn, preset, en, reset
endmodule

module register_file (
  input  clock,
  input  [31:0] C,
  input  Write_enabled,
  input  [1:0] AddrC,
  input  [1:0] AddrA,
  input  [1:0] AddrB,
  input  Read_enabled,
  output [31:0] A,
  output [31:0] B
);

  wire demultiplexer_1_out0, demultiplexer_1_out1, demultiplexer_1_out2, demultiplexer_1_out3;
  wire [31:0] demultiplexer_2_out0, demultiplexer_2_out1, demultiplexer_2_out2, demultiplexer_2_out3, R1_q,
       R2_q, R3_q, R4_q;

  Multiplexer #(.select(2), .width(32)) multiplexer_1 (
    .in0(R1_q), .in1(R2_q), .in2(R3_q), .in3(R4_q), .out(A), .sel(AddrA), .en(Read_enabled));
  Demultiplexer #(.select(2)) demultiplexer_1 (
    .out0(demultiplexer_1_out0), .out1(demultiplexer_1_out1), .out2(demultiplexer_1_out2),
    .out3(demultiplexer_1_out3), .in(1'b1), .sel(AddrC), .en(Write_enabled));
  Demultiplexer #(.select(2), .width(32)) demultiplexer_2 (
    .out0(demultiplexer_2_out0), .out1(demultiplexer_2_out1), .out2(demultiplexer_2_out2),
    .out3(demultiplexer_2_out3), .in(C), .sel(AddrC), .en(Write_enabled));
  Register #(.width(32)) R1 (.D(demultiplexer_2_out0), .en(demultiplexer_1_out0), .Q(R1_q), .clk(clock));  // open: clr
  Register #(.width(32)) R2 (.D(demultiplexer_2_out1), .en(demultiplexer_1_out1), .Q(R2_q), .clk(clock));  // open: clr
  Register #(.width(32)) R3 (.D(demultiplexer_2_out2), .en(demultiplexer_1_out2), .Q(R3_q), .clk(clock));  // open: clr
  Register #(.width(32)) R4 (.D(demultiplexer_2_out3), .en(demultiplexer_1_out3), .Q(R4_q), .clk(clock));  // open: clr
  Multiplexer #(.select(2), .width(32)) multiplexer_2 (
    .in0(R1_q), .in1(R2_q), .in2(R3_q), .in3(R4_q), .out(B), .sel(AddrB), .en(Read_enabled));
endmodule
